# Fritzing sketch beedoh (saved by Fritzing 0.9.3b)
circuit board: 2cm x 2.4cm
breadboards: 1

parts:
  U1 = ESP8266 WiFi Module [part_number=ESP8266]
  IC1 = Voltage Regulator AMS1117 [package=sot223]
  C1 = Electrolytic Capacitor [capacitance=220µF voltage=10V package="100 mil [THT, electrolytic]"]
  C2 = Electrolytic Capacitor [capacitance=1mF voltage=10V package="100 mil [THT, electrolytic]"]
  R4 = Resistor [tolerance=±5% resistance=330 package="0805 [SMD]"]
  R3 = Resistor [tolerance=±5% resistance=680 package="0805 [SMD]"]
  R2 = Resistor [tolerance=±5% resistance=10k package="0805 [SMD]"]
  R1 = Resistor [tolerance=±5% resistance=10k package="0805 [SMD]"]
  R5 = Resistor [tolerance=±5% resistance=22 package="0805 [SMD]"]
  Q1 = PNP-Transistor [package="SOT-23 [SMD]"]
  X1 = USB Connectors [package=usb-minib]
  JP1 = Header 4 [package=jst-4-pth]

nets:
  vcc-3.3: U1.VCC, IC1.OUT, C1.+, R2.Pin_1, R1.Pin_1
  N1: U1.GPIO_0, R3.Pin_0
  N2: U1.RST, R2.Pin_0
  N3: U1.GPIO_2, R4.Pin_0
  N4: U1.CH_PD, R1.Pin_0
  GND: U1.GND, IC1.GND, C1.-, C2.-, Q1.1, X1.GND, JP1.1
  vcc-5.0: IC1.IN, C2.+, X1.VBUS, JP1.2
  N5: R4.Pin_1, JP1.3
  N6: R3.Pin_1, Q1.0
  N7: R5.Pin_0, Q1.2
  N8: R5.Pin_1, JP1.4

notes:
  Bee-Doh, 1

custom parts:
  ESP8266 WiFi Module: Generic WiFi Module based on the ESP8266 with onboard PCB antenna and UART communications
